// Logisim project 1_.circ as structural Verilog: 1 circuit, main circuit main
module main (
  input  in_1,
  input  in_2,
  input  in_3,
  input  in_4,
  output out_5,
  output out_6,
  output out_7,
  output out_8
);

  wire and_1_out, and_2_out, clock_1_out, nand_1_out, nand_2_out, not_1_out;

  Clock clock_1 (.out(clock_1_out));
  not not_1 (not_1_out, in_2);
  and and_1 (and_1_out, not_1_out, in_1);
  and and_2 (and_2_out, in_2, in_1);
  nand nand_1 (nand_1_out, out_8, in_3, clock_1_out);
  nand nand_2 (nand_2_out, clock_1_out, in_4, out_7);
  nor nor_1 (out_5, and_1_out, out_6);
  nor nor_2 (out_6, out_5, and_2_out);
  nand nand_3 (out_7, nand_1_out, out_8);
  nand nand_4 (out_8, out_7, nand_2_out);

  // Notes on the sheet:
  //   D Latch
  //   Flip Flop
endmodule
