// Logisim project 2_.circ as structural Verilog: 1 circuit, main circuit main
module main (
  input  in_1,
  input  in_2,
  input  in_3,
  input  in_4,
  input  in_5,
  input  in_6,
  input  in_7,
  input  in_8,
  input  in_9,
  output out_10,
  output out_11,
  output out_12,
  output out_13,
  output out_14,
  output out_15,
  output out_16,
  output out_17
);

  wire clock_1_out, d_ff_1_q, d_ff_2_q, d_ff_3_q, d_ff_4_q, d_ff_5_q, d_ff_6_q, d_ff_7_q, d_ff_8_q;

  Clock clock_1 (.out(clock_1_out));
  D_Flip_Flop #(.trigger("falling")) d_ff_1 (.D(in_1), .clk(clock_1_out), .Q(d_ff_1_q));  // open: Qn, preset, reset
  and and_1 (out_10, in_9, d_ff_1_q);
  D_Flip_Flop #(.trigger("falling")) d_ff_2 (.D(in_2), .clk(clock_1_out), .Q(d_ff_2_q));  // open: Qn, preset, reset
  and and_2 (out_11, in_9, d_ff_2_q);
  D_Flip_Flop #(.trigger("falling")) d_ff_3 (.D(in_3), .clk(clock_1_out), .Q(d_ff_3_q));  // open: Qn, preset, reset
  and and_3 (out_12, in_9, d_ff_3_q);
  D_Flip_Flop #(.trigger("falling")) d_ff_4 (.D(in_4), .clk(clock_1_out), .Q(d_ff_4_q));  // open: Qn, preset, reset
  and and_4 (out_13, in_9, d_ff_4_q);
  D_Flip_Flop #(.trigger("falling")) d_ff_5 (.D(in_5), .clk(clock_1_out), .Q(d_ff_5_q));  // open: Qn, preset, reset
  and and_5 (out_14, in_9, d_ff_5_q);
  D_Flip_Flop #(.trigger("falling")) d_ff_6 (.D(in_6), .clk(clock_1_out), .Q(d_ff_6_q));  // open: Qn, preset, reset
  and and_6 (out_15, in_9, d_ff_6_q);
  D_Flip_Flop #(.trigger("falling")) d_ff_7 (.D(in_7), .clk(clock_1_out), .Q(d_ff_7_q));  // open: Qn, preset, reset
  and and_7 (out_16, in_9, d_ff_7_q);
  D_Flip_Flop #(.trigger("falling")) d_ff_8 (.D(in_8), .clk(clock_1_out), .Q(d_ff_8_q));  // open: Qn, preset, reset
  and and_8 (out_17, in_9, d_ff_8_q);
endmodule
