// Logisim project 3_.circ as structural Verilog: 1 circuit, main circuit main
module main (
  input  in_1,
  input  in_2,
  input  in_3,
  input  in_4,
  input  [2:0] in_5,
  output [4:0] out_6,
  output [4:0] out_7,
  output [4:0] out_8
);

  wire and_1_out, and_2_out, and_3_out, and_4_out, and_5_out, decoder_1_out0, decoder_1_out1, decoder_1_out2,
       decoder_1_out3, decoder_1_out4;

  Decoder #(.enable("false"), .select(3)) decoder_1 (
    .out0(decoder_1_out0), .out1(decoder_1_out1), .out2(decoder_1_out2), .out3(decoder_1_out3),
    .out4(decoder_1_out4), .sel(in_5));  // open: out5, out6, out7
  and and_1 (and_1_out, decoder_1_out0, in_4);
  and and_2 (and_2_out, decoder_1_out1, in_4);
  and and_3 (and_3_out, decoder_1_out2, in_4);
  and and_4 (and_4_out, decoder_1_out3, in_4);
  and and_5 (and_5_out, decoder_1_out4, in_4);
  D_Flip_Flop d_ff_1 (.D(in_1), .clk(and_1_out), .Q(out_6[0]), .preset(decoder_1_out0));  // open: Qn, reset
  D_Flip_Flop d_ff_2 (.D(in_1), .clk(and_2_out), .Q(out_6[1]), .preset(decoder_1_out1));  // open: Qn, reset
  D_Flip_Flop d_ff_3 (.D(in_1), .clk(and_3_out), .Q(out_6[2]), .preset(decoder_1_out2));  // open: Qn, reset
  D_Flip_Flop d_ff_4 (.D(in_1), .clk(and_4_out), .Q(out_6[3]), .preset(decoder_1_out3));  // open: Qn, reset
  D_Flip_Flop d_ff_5 (.D(in_1), .clk(and_5_out), .Q(out_6[4]), .preset(decoder_1_out4));  // open: Qn, reset
  D_Flip_Flop d_ff_6 (.D(in_2), .clk(and_1_out), .Q(out_7[0]), .preset(decoder_1_out0));  // open: Qn, reset
  D_Flip_Flop d_ff_7 (.D(in_2), .clk(and_2_out), .Q(out_7[1]), .preset(decoder_1_out1));  // open: Qn, reset
  D_Flip_Flop d_ff_8 (.D(in_2), .clk(and_3_out), .Q(out_7[2]), .preset(decoder_1_out2));  // open: Qn, reset
  D_Flip_Flop d_ff_9 (.D(in_2), .clk(and_4_out), .Q(out_7[3]), .preset(decoder_1_out3));  // open: Qn, reset
  D_Flip_Flop d_ff_10 (.D(in_2), .clk(and_5_out), .Q(out_7[4]), .preset(decoder_1_out4));  // open: Qn, reset
  D_Flip_Flop d_ff_11 (.D(in_3), .clk(and_1_out), .Q(out_8[0]), .preset(decoder_1_out0));  // open: Qn, reset
  D_Flip_Flop d_ff_12 (.D(in_3), .clk(and_2_out), .Q(out_8[1]), .preset(decoder_1_out1));  // open: Qn, reset
  D_Flip_Flop d_ff_13 (.D(in_3), .clk(and_3_out), .Q(out_8[2]), .preset(decoder_1_out2));  // open: Qn, reset
  D_Flip_Flop d_ff_14 (.D(in_3), .clk(and_4_out), .Q(out_8[3]), .preset(decoder_1_out3));  // open: Qn, reset
  D_Flip_Flop d_ff_15 (.D(in_3), .clk(and_5_out), .Q(out_8[4]), .preset(decoder_1_out4));  // open: Qn, reset
endmodule
