// Logisim project 4_.circ as structural Verilog: 1 circuit, main circuit main
module main (
  input  in_1,
  input  in_2,
  input  in_3,
  input  in_4,
  input  in_5,
  input  in_6,
  input  in_7,
  input  in_8,
  input  in_9,
  input  in_10,
  input  in_11,
  input  in_12,
  input  in_13,
  input  in_14,
  input  in_15,
  input  in_16,
  input  in_17,
  input  in_18,
  input  in_19,
  input  in_20,
  input  in_21,
  input  in_22,
  input  in_23,
  input  in_24,
  input  write,
  input  in_26,
  input  in_27,
  input  in_28,
  input  in_29,
  input  in_30,
  input  in_31,
  input  in_32,
  input  in_33,
  output out_34,
  output out_35,
  output out_36,
  output out_37,
  output out_38,
  output out_39,
  output out_40,
  output out_41,
  output out_42,
  output out_43,
  output out_44,
  output out_45,
  output out_46,
  output out_47,
  output out_48,
  output out_49,
  output out_50,
  output out_51,
  output out_52,
  output out_53,
  output out_54,
  output out_55,
  output out_56,
  output out_57,
  output out_58,
  output out_59,
  output out_60,
  output out_61,
  output out_62,
  output out_63,
  output out_64,
  output out_65
);

  wire clock_1_out, d_ff_3_q, d_ff_4_q, d_ff_7_q, d_ff_8_q, d_ff_11_q, d_ff_12_q, d_ff_15_q, d_ff_16_q,
       d_ff_19_q, d_ff_20_q, d_ff_23_q, d_ff_24_q, d_ff_27_q, d_ff_28_q, d_ff_31_q, d_ff_32_q;

  Clock clock_1 (.out(clock_1_out));
  D_Flip_Flop #(.trigger("falling")) d_ff_1 (.D(in_1), .clk(clock_1_out), .Q(out_34));  // open: Qn, preset, reset
  D_Flip_Flop #(.trigger("falling")) d_ff_2 (.D(in_9), .clk(clock_1_out), .Q(out_42));  // open: Qn, preset, reset
  D_Flip_Flop #(.trigger("falling")) d_ff_3 (.D(in_17), .clk(clock_1_out), .Q(d_ff_3_q));  // open: Qn, preset, reset
  D_Flip_Flop #(.trigger("falling")) d_ff_4 (.D(in_26), .clk(clock_1_out), .Q(d_ff_4_q));  // open: Qn, preset, reset
  and and_1 (out_50, write, d_ff_3_q);
  and and_2 (out_58, write, d_ff_4_q);
  D_Flip_Flop #(.trigger("falling")) d_ff_5 (.D(in_2), .clk(clock_1_out), .Q(out_35));  // open: Qn, preset, reset
  D_Flip_Flop #(.trigger("falling")) d_ff_6 (.D(in_10), .clk(clock_1_out), .Q(out_43));  // open: Qn, preset, reset
  D_Flip_Flop #(.trigger("falling")) d_ff_7 (.D(in_18), .clk(clock_1_out), .Q(d_ff_7_q));  // open: Qn, preset, reset
  and and_3 (out_51, write, d_ff_7_q);
  D_Flip_Flop #(.trigger("falling")) d_ff_8 (.D(in_27), .clk(clock_1_out), .Q(d_ff_8_q));  // open: Qn, preset, reset
  and and_4 (out_59, write, d_ff_8_q);
  D_Flip_Flop #(.trigger("falling")) d_ff_9 (.D(in_3), .clk(clock_1_out), .Q(out_36));  // open: Qn, preset, reset
  D_Flip_Flop #(.trigger("falling")) d_ff_10 (.D(in_11), .clk(clock_1_out), .Q(out_44));  // open: Qn, preset, reset
  D_Flip_Flop #(.trigger("falling")) d_ff_11 (.D(in_19), .clk(clock_1_out), .Q(d_ff_11_q));  // open: Qn, preset, reset
  D_Flip_Flop #(.trigger("falling")) d_ff_12 (.D(in_28), .clk(clock_1_out), .Q(d_ff_12_q));  // open: Qn, preset, reset
  and and_5 (out_52, write, d_ff_11_q);
  and and_6 (out_60, write, d_ff_12_q);
  D_Flip_Flop #(.trigger("falling")) d_ff_13 (.D(in_4), .clk(clock_1_out), .Q(out_37));  // open: Qn, preset, reset
  D_Flip_Flop #(.trigger("falling")) d_ff_14 (.D(in_12), .clk(clock_1_out), .Q(out_45));  // open: Qn, preset, reset
  D_Flip_Flop #(.trigger("falling")) d_ff_15 (.D(in_20), .clk(clock_1_out), .Q(d_ff_15_q));  // open: Qn, preset, reset
  and and_7 (out_53, write, d_ff_15_q);
  D_Flip_Flop #(.trigger("falling")) d_ff_16 (.D(in_29), .clk(clock_1_out), .Q(d_ff_16_q));  // open: Qn, preset, reset
  and and_8 (out_61, write, d_ff_16_q);
  D_Flip_Flop #(.trigger("falling")) d_ff_17 (.D(in_5), .clk(clock_1_out), .Q(out_38));  // open: Qn, preset, reset
  D_Flip_Flop #(.trigger("falling")) d_ff_18 (.D(in_13), .clk(clock_1_out), .Q(out_46));  // open: Qn, preset, reset
  D_Flip_Flop #(.trigger("falling")) d_ff_19 (.D(in_21), .clk(clock_1_out), .Q(d_ff_19_q));  // open: Qn, preset, reset
  D_Flip_Flop #(.trigger("falling")) d_ff_20 (.D(in_30), .clk(clock_1_out), .Q(d_ff_20_q));  // open: Qn, preset, reset
  and and_9 (out_54, write, d_ff_19_q);
  and and_10 (out_62, write, d_ff_20_q);
  D_Flip_Flop #(.trigger("falling")) d_ff_21 (.D(in_6), .clk(clock_1_out), .Q(out_39));  // open: Qn, preset, reset
  D_Flip_Flop #(.trigger("falling")) d_ff_22 (.D(in_14), .clk(clock_1_out), .Q(out_47));  // open: Qn, preset, reset
  D_Flip_Flop #(.trigger("falling")) d_ff_23 (.D(in_22), .clk(clock_1_out), .Q(d_ff_23_q));  // open: Qn, preset, reset
  D_Flip_Flop #(.trigger("falling")) d_ff_24 (.D(in_31), .clk(clock_1_out), .Q(d_ff_24_q));  // open: Qn, preset, reset
  and and_11 (out_55, write, d_ff_23_q);
  and and_12 (out_63, write, d_ff_24_q);
  D_Flip_Flop #(.trigger("falling")) d_ff_25 (.D(in_7), .clk(clock_1_out), .Q(out_40));  // open: Qn, preset, reset
  D_Flip_Flop #(.trigger("falling")) d_ff_26 (.D(in_15), .clk(clock_1_out), .Q(out_48));  // open: Qn, preset, reset
  D_Flip_Flop #(.trigger("falling")) d_ff_27 (.D(in_23), .clk(clock_1_out), .Q(d_ff_27_q));  // open: Qn, preset, reset
  and and_13 (out_56, write, d_ff_27_q);
  D_Flip_Flop #(.trigger("falling")) d_ff_28 (.D(in_32), .clk(clock_1_out), .Q(d_ff_28_q));  // open: Qn, preset, reset
  and and_14 (out_64, write, d_ff_28_q);
  D_Flip_Flop #(.trigger("falling")) d_ff_29 (.D(in_8), .clk(clock_1_out), .Q(out_41));  // open: Qn, preset, reset
  D_Flip_Flop #(.trigger("falling")) d_ff_30 (.D(in_16), .clk(clock_1_out), .Q(out_49));  // open: Qn, preset, reset
  D_Flip_Flop #(.trigger("falling")) d_ff_31 (.D(in_24), .clk(clock_1_out), .Q(d_ff_31_q));  // open: Qn, preset, reset
  D_Flip_Flop #(.trigger("falling")) d_ff_32 (.D(in_33), .clk(clock_1_out), .Q(d_ff_32_q));  // open: Qn, preset, reset
  and and_15 (out_57, write, d_ff_31_q);
  and and_16 (out_65, write, d_ff_32_q);
endmodule
